# Fritzing sketch star-wars-macro-keyboard (saved by Fritzing 0.9.3b)

parts:
  Armed_LED = LED - 5mm [color="Red (633nm)" package="5 mm [THT]"]
  LED_V1 = LED - 3mm [color="White (4500K)" package="3 mm [THT]"]
  LED_V2 = LED - 3mm [color="White (4500K)" package="3 mm [THT]"]
  R1 = Resistor [tolerance=±5% resistance=220 package="2010 [SMD]"]
  R2 = Resistor [tolerance=±5% resistance=220 package="2010 [SMD]"]
  Part1 = Arduino Pro Micro (Clone)
  H3 = Momentary Switch [package=ksa_sealed_tac_switch]
  H2 = Momentary Switch [package=ksa_sealed_tac_switch]
  H1 = Momentary Switch [package=ksa_sealed_tac_switch]
  Armed_button = Round Pushbutton
  R3 = Resistor [tolerance=±5% resistance=220 package="2010 [SMD]"]
  V1 = Momentary Switch [package=ksa_sealed_tac_switch]
  V2 = Momentary Switch [package=ksa_sealed_tac_switch]

nets:
  N1: Armed_LED.cathode, Part1.GND, H3.1, Armed_button.leg0, V2.2
  N2: Armed_LED.anode, R3.Pin_1
  N3: LED_V1.cathode, LED_V2.cathode
  N4: LED_V1.anode, R2.Pin_1
  N5: LED_V2.anode, R1.Pin_1
  N6: R1.Pin_0, Part1.D9
  N7: R2.Pin_0, Part1.D10
  N8: Part1.D2, R3.Pin_0
  N9: Part1.D3, Armed_button.leg1
  N10: Part1.D4, H1.3
  N11: Part1.D5, H2.3
  N12: Part1.D6, H3.3
  N13: Part1.D7, V2.4
  N14: Part1.D8, V1.4
  N15: H3.2, H2.1
  N16: H2.2, H1.1
  N17: V1.1, V2.1
